# Fritzing sketch board (saved by Fritzing 0.9.6b)
breadboards: 1

parts:
  LED1 = LED - 5mm [color="Red (633nm)" current=0.030 package="5 mm [THT]"]
  R1 = Resistor [tolerance=±5% resistance=220 package="2010 [SMD]"]
  Part1 = Arduino Uno (Rev3)

nets:
  N1: LED1.cathode, Part1.GND
  N2: LED1.anode, R1.Pin_1
  N3: R1.Pin_0, Part1.D4

// code stored in the sketch: arduino_uno.ino
const int pwm = 2 ; 		
void setup()
{
     pinMode(pwm,OUTPUT) ; 	//Set pin 2 as output
}
void loop()
{
     analogWrite(pwm,200) ; 		 //setting pwm to 25 
     delay(1000) ; // delay 1s
		 analogWrite(pwm,0); 		
}
